# Fritzing sketch lab2connections (saved by Fritzing 0.9.3b)
breadboards: 1

parts:
  Part1 = Adafruit Pi Cobbler Plus [part_number="Adafruit #2029"]
  DHT1 = DHT22 Humidity and Temperature Sensor
  R1 = Resistor [tolerance=±5% resistance=560 package="2512 [SMD]"]
  R2 = Resistor [tolerance=±5% resistance=10k package="2512 [SMD]"]
  LED1 = smd LED [color="Green (555nm)" package="0603 [SMD]"]
  JP1 = Header 8 [package=1x08_smd]
  USBTTL1 = USB TTL Serial Cable

nets:
  N1: Part1.GPIO6, DHT1.DATA, R2.Pin_1
  N2: Part1.GPIO19, R1.Pin_0
  N3: DHT1.VDD, R2.Pin_0, JP1.1
  GND: DHT1.GND, LED1.cathode, JP1.3, USBTTL1.GND
  N4: R1.Pin_1, LED1.anode
  N5: JP1.4, USBTTL1.RX
  N6: JP1.5, USBTTL1.TX

custom parts:
  Adafruit Pi Cobbler Plus: The Raspberry Pi B+/Pi 2/ Pi 3 has landed on the Maker World like a 40-GPIO pinned, quad-USB ported, credit card sized bomb of DIY joy. And while you can use most of our great Model B accessories by hooking up our downgrade cable, its probably a good time to upgrade your set up and accessorize using all of the Model B+'s / Pi 2's / Pi 3's 40 pins. That's why we now carry the Adafruit Assembled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
